# Fritzing sketch arduino proyecto 1 (saved by Fritzing 0.8.7b)
circuit board: 11.1776cm x 6.08214cm

parts:
  Parte1 = Arduino Mega ADK (Rev3)
  Parte2 = Bluetooth HC-05 Macho
  KY-1 = Keyes Relay [package=THT]

nets (from the breadboard view):
  GND: Parte1.GND, Parte2.GND, KY-1.ground
  5V: Parte1.IOREF, Parte1.5V, Parte2.VCC, KY-1.power
  N1: Parte1.D0/RX0, Parte2.TXD
  N2: Parte1.D1/TX0, Parte2.RXD
  N3: Parte1.D2_PWM, KY-1.signal

notes:
  arduino

custom parts:
  Keyes Relay: The Keyes 5V relay module is suitable for SCM development, home appliance control. It uses a 5V~12V TIL control signal which can control DC / AC signal.
